# Fritzing sketch Task 8.2HD Sketch (saved by Fritzing 1.0.2b)
breadboards: 2

parts:
  M2 = Arduino Nano 33 IOT-smd
  HC-SR04_Sensor_1 = HC-SR04 Ultrasonic Distance Sensor
  Part1 = Logic Level Converter
  YwRobot_Power_Supply1 = YwRobot Breadboard Power Supply [part_number=545043]
  LED1 = LED - 5mm [color="Green (565nm)" current=0.030A package="5 mm [THT]"]
  R1 = Resistor [tolerance=±5% power=0.25W resistance=1000 package=THT]
  Mod2 = Raspberry Pi 4B  # not connected
  LED3 = LED - 5mm [color="Green (555nm)" current=0.030A package="5 mm [THT]"]
  Part2 = Adafruit T-Cobbler Plus [part_number="Adafruit #1989 and #2028"]
  R3 = Resistor [tolerance=±5% power=0.25W resistance=1k package=THT]
  LED4 = LED - 5mm [color="Red (633nm)" current=0.030A package="5 mm [THT]"]
  J1 = Piezo Speaker
  Q1 = NPN-Transistor [package="TO92 [THT]"]

nets:
  N1: M2.pin_13, M2.pin_18
  N2: M2.pin_14, M2.pin_19, YwRobot_Power_Supply1.VCC#10, LED1.anode, LED4.anode, Q1.C
  N3: M2.pin_20, R1.Pin_1
  N4: M2.pin_21, LED4.cathode
  N5: M2.pin_22, LED1.cathode
  VCC: HC-SR04_Sensor_1.VCC, Part1.HV, Part2.+5V
  N6: HC-SR04_Sensor_1.TRIG, Part2.GPIO18
  N7: HC-SR04_Sensor_1.ECHO, Part1.RX2_HV
  GND: HC-SR04_Sensor_1.GND, Part1.GND, Part2.GND, R3.Pin_1
  N8: Part1.RX2_LV, Part2.GPIO24
  N9: Part1.LV, Part2.+3.3V
  N10: YwRobot_Power_Supply1.GND#14, J1.pin2
  N11: R1.Pin_0, Q1.B
  N12: LED3.cathode, Part2.GPIO26
  N13: LED3.anode, R3.Pin_0
  N14: J1.pin1, Q1.E

custom parts:
  Arduino Nano 33 IOT-smd: The Arduino Nano 33 IoT is the easiest and cheapest point of entry to enhance existing devices (and creating new ones) to be part of the IoT and designing pico-network applications. Whether you are looking at building a sensor network connected to your office or home router, or if you want to create a BLE device sending data to a cellphone, the Nano 33 IoT is your one-stop-solution for many of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
  YwRobot Breadboard Power Supply: The YwRobot Breadboard Power Supply (MB-V2) has two power rails; they can be 5V or 3V3. Power to the module can be provided through the female USB socket or through the A10 (female) 2.1mm power jack.
  Adafruit T-Cobbler Plus: The Raspberry Pi has landed on the Maker World like a 40-GPIO pinned, quad-USB ported, credit card sized bomb of DIY joy. And while you can use most of our great Model B accessories by hooking up our downgrade cable, its probably a good time to upgrade your set up and accessorize using all of the 40 pins. That's why we now carry the Assembled Adafruit Pi T-Cobbler Plus - Breakout + Cable for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
